# Fritzing sketch rpi3_schematics (saved by Fritzing 0.9.3b)
breadboards: 1

parts:
  R2 = Resistor [tolerance=±5% resistance=470 package="0402 [SMD]"]
  LED1 = smd LED [color="Red (633nm)" package="1206 [SMD]"]
  Raspberry_Pi_1 = Raspberry Pi 3 [part_number=RPI-3-V1.2]

nets:
  N1: R2.Pin_0, Raspberry_Pi_1.GPIO21
  N2: R2.Pin_1, LED1.anode
  N3: LED1.cathode, Raspberry_Pi_1.GND
